# Fritzing sketch diagram (saved by Fritzing 0.9.3b)
breadboards: 1

parts:
  Q2 = PHOTOTRANSISTOR REFLECTIVE OBJECT SENSOR [package=qrb1114-side]
  R1 = Resistor [tolerance=±5% resistance=10k package=THT]
  R2 = Resistor [tolerance=±5% resistance=200 package=THT]
  M1 = DC Motor
  M2 = DC Motor
  Q1 = PHOTOTRANSISTOR REFLECTIVE OBJECT SENSOR [package=qrb1114-side]
  R4 = Resistor [tolerance=±5% resistance=200 package=THT]
  R3 = Resistor [tolerance=±5% resistance=10k package=THT]
  Part1 = Arduino Uno (Rev3) - ICSP
  Part2 = Adafruit Motor/Stepper/Servo Shield [part_number="Adafruit #1438"]

nets:
  N1: Q2.A, R2.Pin_0
  N2: Q2.C, R1.Pin_0, Part1.A0
  GND: Q2.E, Q2.K, Q1.E, Q1.K
  N3: R1.Pin_1, R2.Pin_1, R4.Pin_1, R3.Pin_1, Part1.5V
  N4: M1.pin_1, Part2.M2B
  N5: M1.pin_2, Part2.M2A
  N6: M2.pin_1, Part2.M3B
  N7: M2.pin_2, Part2.M3A
  N8: Q1.A, R4.Pin_0
  N9: Q1.C, R3.Pin_0, Part1.A1

custom parts:
  Adafruit Motor/Stepper/Servo Shield: The original Adafruit Motorshield kit is one of our most beloved kits, which is why we decided to make something even better. We have upgraded the shield kit to make the bestest, easiest way to drive DC and Stepper motors. This shield will make quick work of your next robotics project! We kept the ability to drive up to 4 DC motors or 2 stepper motors, but added many improvements: Instead of a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
